// Logisim project ALU.circ as structural Verilog: 14 circuits, main circuit Ida ALU
// ALU
module Ida_ALU (
  input  [23:0] ALU_Source_1,
  input  [23:0] ALU_Source_2,
  input  [3:0] Operation,
  output [23:0] ALU_Result
);

  wire [4:0] s2_5bits;
  wire [23:0] ADD_8, AND_5, CMPS_12, CMPU_13, IOR_6, RTL_3, RTR_4, SAR_2, SLL_0, SRL_1, SUB_9, XOR_7;

  // Probe on ALU_Source_1
  // Probe on ALU_Source_2
  // Probe on Operation
  // Probe on ALU_Result
  SLL sll_1 (.in_1(ALU_Source_1), .in_2(s2_5bits), .out_3(SLL_0));
  SLR slr_1 (.in_1(ALU_Source_1), .in_2(s2_5bits), .out_3(SRL_1));
  SAR sar_1 (.in_1(ALU_Source_1), .in_2(s2_5bits), .out_3(SAR_2));
  RTL rtl_1 (.in_1(ALU_Source_1), .in_2(s2_5bits), .out_3(RTL_3));
  RTR rtr_1 (.in_1(ALU_Source_1), .in_2(s2_5bits), .out_3(RTR_4));
  AND and_1 (.in_1(ALU_Source_1), .in_2(ALU_Source_2), .out_3(AND_5));
  IOR ior_1 (.in_1(ALU_Source_1), .in_2(ALU_Source_2), .out_3(IOR_6));
  XOR xor_1 (.in_1(ALU_Source_1), .in_2(ALU_Source_2), .out_3(XOR_7));
  ADD add_1 (.in_1(ALU_Source_1), .in_2(ALU_Source_2), .out_3(ADD_8));
  SUB sub_1 (.in_1(ALU_Source_1), .in_2(ALU_Source_2), .out_3(SUB_9));
  CMPS cmps_1 (.A(ALU_Source_1), .B(ALU_Source_2), .Output(CMPS_12));
  CMPU cmpu_1 (.A(ALU_Source_1), .B(ALU_Source_2), .Output(CMPU_13));
  Bit_Extender #(.in_width(24), .out_width(5)) bit_extender_1 (.in(ALU_Source_2), .out(s2_5bits));
  Multiplexer #(.select(4), .width(24), .enable("false")) multiplexer_1 (
    .in0(SLL_0), .in1(SRL_1), .in2(SAR_2), .in3(RTL_3), .in4(RTR_4), .in5(AND_5), .in6(IOR_6), .in7(XOR_7),
    .in8(ADD_8), .in9(SUB_9), .in10(ADD_8), .in11(ADD_8), .in12(CMPS_12), .in13(CMPU_13), .in14({24{1'b0}}),
    .in15({24{1'b0}}), .out(ALU_Result), .sel(Operation));

  // Other names for the same wires on the sheet: op[3:0] = Operation; result[23:0] = ALU_Result;
  //   s1[23:0] = ALU_Source_1; s2[23:0] = ALU_Source_2

  // Notes on the sheet:
  //   INPUTS
  //   INPUT PROBES
  //   DO NOT MOVE/ADD/CHANGE ANY INPUT OR OUTPUT PINS!
  //   OUTPUT PROBES
  //   OUTPUT
endmodule

module SLL (
  input  [23:0] in_1,
  input  [4:0] in_2,
  output [23:0] out_3
);

  Shifter #(.width(24)) shifter_1 (.in(in_1), .\dist (in_2), .out(out_3));
endmodule

module SLR (
  input  [23:0] in_1,
  input  [4:0] in_2,
  output [23:0] out_3
);

  Shifter #(.width(24), .shift("lr")) shifter_1 (.in(in_1), .\dist (in_2), .out(out_3));
endmodule

module SAR (
  input  [23:0] in_1,
  input  [4:0] in_2,
  output [23:0] out_3
);

  Shifter #(.width(24), .shift("ar")) shifter_1 (.in(in_1), .\dist (in_2), .out(out_3));
endmodule

module RTL (
  input  [23:0] in_1,
  input  [4:0] in_2,
  output [23:0] out_3
);

  Shifter #(.width(24), .shift("rl")) shifter_1 (.in(in_1), .\dist (in_2), .out(out_3));
endmodule

module RTR (
  input  [23:0] in_1,
  input  [4:0] in_2,
  output [23:0] out_3
);

  Shifter #(.width(24), .shift("rr")) shifter_1 (.in(in_1), .\dist (in_2), .out(out_3));
endmodule

module AND (
  input  [23:0] in_1,
  input  [23:0] in_2,
  output [23:0] out_3
);

  assign out_3 = in_1 & in_2;  // AND_Gate and_1, 24 bits wide
endmodule

module IOR (
  input  [23:0] in_1,
  input  [23:0] in_2,
  output [23:0] out_3
);

  assign out_3 = in_1 | in_2;  // OR_Gate or_1, 24 bits wide
endmodule

module XOR (
  input  [23:0] in_1,
  input  [23:0] in_2,
  output [23:0] out_3
);

  assign out_3 = in_1 ^ in_2;  // XOR_Gate xor_1, 24 bits wide
endmodule

module ADD (
  input  [23:0] in_1,
  input  [23:0] in_2,
  output [23:0] out_3
);

  Adder #(.width(24)) adder_1 (.a(in_1), .b(in_2), .out(out_3));  // open: cin, cout
endmodule

module SUB (
  input  [23:0] in_1,
  input  [23:0] in_2,
  output [23:0] out_3
);

  Subtractor #(.width(24)) subtractor_1 (.a(in_1), .b(in_2), .out(out_3));  // open: bin, bout
endmodule

module CMPS (
  input  [23:0] A,
  input  [23:0] B,
  output [23:0] Output
);

  wire comparator_1_eq, comparator_1_gt, comparator_1_lt;

  Comparator #(.width(24)) comparator_1 (
    .a(A), .b(B), .gt(comparator_1_gt), .eq(comparator_1_eq), .lt(comparator_1_lt));
  CompEncoder compencoder_1 (
    .Greater(comparator_1_gt), .Equal(comparator_1_eq), .Less(comparator_1_lt), .Output(Output));
endmodule

module CMPU (
  input  [23:0] A,
  input  [23:0] B,
  output [23:0] Output
);

  wire comparator_1_eq, comparator_1_gt, comparator_1_lt;

  Comparator #(.width(24), .mode("unsigned")) comparator_1 (
    .a(A), .b(B), .gt(comparator_1_gt), .eq(comparator_1_eq), .lt(comparator_1_lt));
  CompEncoder compencoder_1 (
    .Greater(comparator_1_gt), .Equal(comparator_1_eq), .Less(comparator_1_lt), .Output(Output));
endmodule

module CompEncoder (
  input  Greater,
  input  Equal,
  input  Less,
  output [23:0] Output
);

  wire [1:0] and_1_out, and_2_out, and_3_out, bit_extender_1_out, bit_extender_2_out, bit_extender_3_out,
       or_1_out;

  assign bit_extender_1_out = {{1{Greater}}, Greater};  // Bit_Extender bit_extender_1
  assign bit_extender_2_out = {{1{Equal}}, Equal};  // Bit_Extender bit_extender_2
  assign bit_extender_3_out = {{1{Less}}, Less};  // Bit_Extender bit_extender_3
  assign and_1_out = bit_extender_1_out & 2'b01;  // AND_Gate and_1, 2 bits wide
  assign and_2_out = bit_extender_2_out & 2'b10;  // AND_Gate and_2, 2 bits wide
  assign and_3_out = bit_extender_3_out & 2'b11;  // AND_Gate and_3, 2 bits wide
  assign or_1_out = and_1_out | and_2_out | and_3_out;  // OR_Gate or_1, 2 bits wide
  assign Output = {{22{1'b0}}, or_1_out};  // Bit_Extender bit_extender_4
endmodule
