// Logisim project CPU.circ as structural Verilog: 4 circuits, main circuit Ida CPU
// CPU
module Ida_CPU (
  input  [31:0] Instruction,
  input  Clock,
  output [23:0] Mem_Data,
  output [23:0] Mem_Address,
  output Mem_Write,
  output [23:0] Next_PC,
  output [23:0] r00,
  output [23:0] r01,
  output [23:0] r02,
  output [23:0] r03,
  output [23:0] r04,
  output [23:0] r05,
  output [23:0] r06,
  output [23:0] r07,
  output [23:0] r08,
  output [23:0] r09,
  output [23:0] r10,
  output [23:0] r11,
  output [23:0] r12,
  output [23:0] r13,
  output [23:0] r14,
  output [23:0] r15
);

  wire A2_Type, CQControl_execute, IMM, Jump, JumpReg, Link, memToReg, RegWrite;
  wire [1:0] bit_extender_2_out, CR;
  wire [3:0] multiplexer_2_out, Read1, Read3Write;
  wire [23:0] adder_1_out, bit_extender_1_out, ida_register_file_1_reg_1_value,
       ida_register_file_1_reg_2_value, Immidiate, JUMPAddress, multiplexer_5_out, multiplexer_7_out,
       multiplexer_10_out, ram_1_data, WriteVal;
  wire [31:0] InstExec, multiplexer_6_out, prevInst;

  // Probe on Instruction
  // Probe on Clock
  // Probe on r00
  // Probe on r01
  // Probe on r02
  // Probe on r03
  // Probe on r04
  // Probe on r05
  // Probe on r06
  // Probe on r07
  // Probe on Mem_Data
  // Probe on Mem_Address
  // Probe on Mem_Write
  // Probe on Next_PC
  // Probe on WriteVal
  // Probe on JUMPAddress
  // Probe on InstExec[31:28]
  // Probe on Mem_Data
  // Probe on r08
  // Probe on r09
  // Probe on r10
  // Probe on r11
  // Probe on r12
  // Probe on r13
  // Probe on r14
  // Probe on r15
  Ida_Register_File ida_register_file_1 (
    .Read_Reg_1(Read1), .Read_Reg_2(InstExec[3:0]), .Write_Reg(Read3Write), .Write_Value(WriteVal),
    .Reg_1_Value(ida_register_file_1_reg_1_value), .Reg_2_Value(ida_register_file_1_reg_2_value),
    .Reg_Write(RegWrite), .Clock(Clock), .r00(r00), .r01(r01), .r02(r02), .r03(r03), .r04(r04), .r05(r05),
    .r06(r06), .r07(r07), .r08(r08), .r09(r09), .r10(r10), .r11(r11), .r12(r12), .r13(r13), .r14(r14),
    .r15(r15), .Reg_3_Value(Mem_Data));
  Bit_Extender #(.in_width(32), .out_width(24)) bit_extender_1 (
    .in({InstExec[31:25], IMM, InstExec[23:0]}), .out(bit_extender_1_out));
  Multiplexer #(.width(4), .enable("false")) multiplexer_1 (
    .in0(InstExec[19:16]), .in1(InstExec[23:20]), .out(Read1), .sel(A2_Type));
  Multiplexer #(.width(4), .enable("false")) multiplexer_2 (
    .in0(InstExec[23:20]), .in1(4'b0010), .out(multiplexer_2_out), .sel(Link));
  Multiplexer #(.width(4), .enable("false")) multiplexer_3 (
    .in0(multiplexer_2_out), .in1(4'b0010), .out(Read3Write), .sel(JumpReg));
  A_Type_Imm a_type_imm_1 (.optcode(InstExec[31:28]), .Immidiate(bit_extender_1_out), .RI(Immidiate));
  Multiplexer #(.width(24), .enable("false")) multiplexer_4 (
    .in0(Immidiate), .in1(Mem_Data), .out(JUMPAddress), .sel(JumpReg));
  Multiplexer #(.width(24), .enable("false")) multiplexer_5 (
    .in0(ida_register_file_1_reg_2_value), .in1(Immidiate), .out(multiplexer_5_out), .sel(IMM));
  Ida_ALU ida_alu_1 (
    .ALU_Source_1(ida_register_file_1_reg_1_value), .ALU_Source_2(multiplexer_5_out),
    .Operation(InstExec[31:28]), .ALU_Result(Mem_Address));
  Control control_1 (
    .Op_code(InstExec[31:28]), .IMM(IMM), .A2_Type(A2_Type), .RegWrite(RegWrite), .MemWrite(Mem_Write),
    .MemToReg(memToReg), .Jump(Jump), .Link(Link), .JumpReg(JumpReg));
  Multiplexer #(.width(32), .enable("false")) multiplexer_6 (
    .in0(Instruction), .in1({32{1'b0}}), .out(multiplexer_6_out), .sel(Jump));
  Register #(.width(32)) Pipeline (.D(multiplexer_6_out), .Q(prevInst), .clk(Clock));  // open: en, clr
  RAM #(.addrWidth(24), .dataWidth(24), .bus("separate")) ram_1 (
    .addr(Mem_Address), .din(Mem_Data), .data(ram_1_data), .str(Mem_Write), .clk(Clock));  // open: sel, ld, clr
  Multiplexer #(.width(24), .enable("false")) multiplexer_7 (
    .in0(Mem_Address), .in1(ram_1_data), .out(multiplexer_7_out), .sel(memToReg));
  Bit_Extender #(.in_width(24), .out_width(2)) bit_extender_2 (.in(WriteVal), .out(bit_extender_2_out));
  CQControl CQControl (.CR(CR), .CQ(prevInst[27:25]), .Execute(CQControl_execute));
  Adder #(.width(24)) adder_1 (.a(24'h1), .b(Next_PC), .out(adder_1_out));  // open: cin, cout
  Multiplexer #(.width(24), .enable("false")) multiplexer_8 (
    .in0(multiplexer_7_out), .in1(Immidiate), .out(WriteVal), .sel(Link));
  Register #(.width(2)) u_CR (.D(bit_extender_2_out), .en(A2_Type), .Q(CR), .clk(Clock));  // open: clr
  Multiplexer #(.width(32), .enable("false")) multiplexer_9 (
    .in0({32{1'b0}}), .in1(prevInst), .out({InstExec[31:25], IMM, InstExec[23:0]}), .sel(CQControl_execute));
  Register #(.width(24)) PC (.D(multiplexer_10_out), .Q(Next_PC), .clk(Clock));  // open: en, clr
  Multiplexer #(.width(24), .enable("false")) multiplexer_10 (
    .in0(adder_1_out), .in1(JUMPAddress), .out(multiplexer_10_out), .sel(Jump));

  // Other names for the same wires on the sheet: clk = Clock; inst[31:0] = Instruction; Read2[3:0] = InstExec[3:0];
  //   InstExec[24] = IMM; Opcode[3:0] = InstExec[31:28]; memAddr[23:0] = Mem_Address; memData[23:0] = Mem_Data;
  //   memWrite = Mem_Write; nextPC[23:0] = Next_PC

  // Notes on the sheet:
  //   INPUTS
  //   INPUT PROBES
  //   OUTPUT PROBES
  //   OUTPUTS
  //   DO NOT MOVE/ADD/CHANGE ANY INPUT OR OUTPUT PINS!
  //   Decoder
  //   RS
  //   RD
  //   RI
  //   Controler
  //   Pipelining
  //   CR
  //   ?CQ Controler
  //   PC
endmodule

module Control (
  input  [3:0] Op_code,
  input  IMM,
  output A2_Type,
  output RegWrite,
  output MemWrite,
  output MemToReg,
  output Jump,
  output Link,
  output JumpReg
);

  wire CMPS, CMPU, not_1_out, not_2_out, not_3_out, not_4_out, not_5_out, not_6_out, not_7_out, not_8_out,
       or_2_out;

  not not_1 (not_1_out, Op_code[0]);
  not not_2 (not_2_out, Op_code[1]);
  not not_3 (not_3_out, Op_code[1]);
  not not_4 (not_4_out, IMM);
  and and_1 (Jump, Op_code[0], Op_code[1], Op_code[2], Op_code[3]);
  and and_2 (CMPS, not_1_out, not_2_out, Op_code[2], Op_code[3]);
  and and_3 (CMPU, Op_code[0], not_3_out, Op_code[2], Op_code[3]);
  and and_4 (JumpReg, Jump, not_4_out);
  not not_5 (not_5_out, Op_code[0]);
  not not_6 (not_6_out, Op_code[2]);
  not not_7 (not_7_out, Op_code[0]);
  not not_8 (not_8_out, Op_code[2]);
  and and_5 (Link, not_5_out, Op_code[1], Op_code[2], Op_code[3]);
  and and_6 (MemWrite, Op_code[0], Op_code[1], not_6_out, Op_code[3]);
  and and_7 (MemToReg, not_7_out, Op_code[1], not_8_out, Op_code[3]);
  or or_1 (A2_Type, CMPS, CMPU);
  or or_2 (or_2_out, CMPS, CMPU, MemWrite, Jump);
  not not_9 (RegWrite, or_2_out);

  // Other names for the same wires on the sheet: LOAD = MemToReg; op_0 = Op_code[0]; op_1 = Op_code[1];
  //   op_2 = Op_code[2]; op_3 = Op_code[3]; SAVE = MemWrite

  // Notes on the sheet:
  //   AND
  //   OR
endmodule

module A_Type_Imm (
  input  [3:0] optcode,
  input  [23:0] Immidiate,
  output [23:0] RI
);

  wire [15:0] bit_extender_1_out;
  wire [19:0] bit_extender_2_out;
  wire [23:0] bit_extender_3_out, bit_extender_4_out;

  Bit_Extender #(.in_width(24)) bit_extender_1 (.in(Immidiate), .out(bit_extender_1_out));
  Bit_Extender #(.in_width(24), .out_width(20)) bit_extender_2 (.in(Immidiate), .out(bit_extender_2_out));
  assign bit_extender_3_out = {{8{bit_extender_1_out[15]}}, bit_extender_1_out};  // Bit_Extender bit_extender_3
  assign bit_extender_4_out = {{4{bit_extender_2_out[19]}}, bit_extender_2_out};  // Bit_Extender bit_extender_4
  Multiplexer #(.select(4), .width(24), .enable("false")) multiplexer_1 (
    .in0(bit_extender_3_out), .in1(bit_extender_3_out), .in2(bit_extender_3_out), .in3(bit_extender_3_out),
    .in4(bit_extender_3_out), .in5(bit_extender_3_out), .in6(bit_extender_3_out), .in7(bit_extender_3_out),
    .in8(bit_extender_3_out), .in9(bit_extender_3_out), .in10(bit_extender_3_out), .in11(bit_extender_3_out),
    .in12(bit_extender_4_out), .in13(bit_extender_4_out), .in14(Immidiate), .in15(Immidiate), .out(RI),
    .sel(optcode));

  // Notes on the sheet:
  //   A3-Type
  //   A2-Type
  //   A1-Type
endmodule

module CQControl (
  input  [1:0] CR,
  input  [2:0] CQ,
  output Execute
);

  wire and_7_out, EQ, Equal, Equal_CR, GE, GE_CR, Greater, Greater_CR, GreaterOrEqual, GT, LE, LE_CR, Less,
       Less_CR, LessOrEqual, LT, NE, NO, not_1_out, not_2_out, NotEqual, OK, or_3_out, Start;

  Demultiplexer #(.select(2)) demultiplexer_1 (
    .out0(Start), .out1(Greater_CR), .out2(Equal_CR), .out3(Less_CR), .in(1'b1), .sel(CR));  // open: en
  or or_1 (LE_CR, Equal_CR, Less_CR);
  and and_1 (LessOrEqual, LE, LE_CR);
  and and_2 (GreaterOrEqual, GE, GE_CR);
  and and_3 (Less, LT, Less_CR);
  or or_2 (GE_CR, Equal_CR, Greater_CR);
  not not_1 (not_1_out, Equal_CR);
  Demultiplexer #(.select(3)) demultiplexer_2 (
    .out0(NO), .out1(LE), .out2(GT), .out3(NE), .out4(EQ), .out5(GE), .out6(LT), .out7(OK), .in(1'b1),
    .sel(CQ));  // open: en
  and and_4 (Equal, EQ, Equal_CR);
  and and_5 (NotEqual, NE, not_1_out);
  and and_6 (Greater, GT, Greater_CR);
  or or_3 (or_3_out, Equal, GreaterOrEqual, NotEqual, LessOrEqual, Less, Greater);
  not not_2 (not_2_out, Start);
  and and_7 (and_7_out, or_3_out, not_2_out);
  or or_4 (Execute, and_7_out, OK);

  // Notes on the sheet:
  //   AND
  //   OR
endmodule
