// Logisim project REG.circ as structural Verilog: 2 circuits, main circuit Ida Register File
// Register File
module Ida_Register_File (
  input  [3:0] Read_Reg_1,
  input  [3:0] Read_Reg_2,
  input  [3:0] Write_Reg,
  input  [23:0] Write_Value,
  input  Reg_Write,
  input  Clock,
  output [23:0] Reg_1_Value,
  output [23:0] Reg_2_Value,
  output [23:0] Reg_3_Value,
  output [23:0] r00,
  output [23:0] r01,
  output [23:0] r02,
  output [23:0] r03,
  output [23:0] r04,
  output [23:0] r05,
  output [23:0] r06,
  output [23:0] r07,
  output [23:0] r08,
  output [23:0] r09,
  output [23:0] r10,
  output [23:0] r11,
  output [23:0] r12,
  output [23:0] r13,
  output [23:0] r14,
  output [23:0] r15
);

  wire and_1_out, R01_Enab, R02_Enab, R03_Enab, R04_Enab, R05_Enab, R06_Enab, R07_Enab, R08_Enab, R09_Enab,
       R10_Enab, R11_Enab, R12_Enab, R13_Enab, R14_Enab, R15_Enab;

  // Probe on Read_Reg_1
  // Probe on Read_Reg_2
  // Probe on Write_Reg
  // Probe on Write_Value
  // Probe on Reg_Write
  // Probe on Clock
  // Probe on Reg_1_Value
  // Probe on Reg_2_Value
  // Probe on Reg_3_Value
  // Probe on r00
  // Probe on r01
  // Probe on r02
  // Probe on r03
  // Probe on r04
  // Probe on r05
  // Probe on r06
  // Probe on r07
  // Probe on r08
  // Probe on r09
  // Probe on r10
  // Probe on r11
  // Probe on r12
  // Probe on r13
  // Probe on r14
  // Probe on r15
  readRegister readregister_1 (
    .r15(r15), .r14(r14), .r13(r13), .r12(r12), .r11(r11), .r10(r10), .r09(r09), .r08(r08), .r07(r07),
    .r06(r06), .r05(r05), .r04(r04), .r03(r03), .r02(r02), .r01(r01), .r00(r00), .ReadReg(Read_Reg_1),
    .Output(Reg_1_Value));
  Register #(.width(24)) u_R00 (.D(Write_Value), .en(1'b0), .Q(r00), .clk(Clock));  // open: clr
  Register #(.width(24)) u_R04 (.D(Write_Value), .en(R04_Enab), .Q(r04), .clk(Clock));  // open: clr
  Register #(.width(24)) u_R08 (.D(Write_Value), .en(R08_Enab), .Q(r08), .clk(Clock));  // open: clr
  Register #(.width(24)) u_R12 (.D(Write_Value), .en(R12_Enab), .Q(r12), .clk(Clock));  // open: clr
  readRegister readregister_2 (
    .r15(r15), .r14(r14), .r13(r13), .r12(r12), .r11(r11), .r10(r10), .r09(r09), .r08(r08), .r07(r07),
    .r06(r06), .r05(r05), .r04(r04), .r03(r03), .r02(r02), .r01(r01), .r00(r00), .ReadReg(Read_Reg_2),
    .Output(Reg_2_Value));
  Register #(.width(24)) u_R01 (.D(Write_Value), .en(R01_Enab), .Q(r01), .clk(Clock));  // open: clr
  Register #(.width(24)) u_R05 (.D(Write_Value), .en(R05_Enab), .Q(r05), .clk(Clock));  // open: clr
  Register #(.width(24)) u_R09 (.D(Write_Value), .en(R09_Enab), .Q(r09), .clk(Clock));  // open: clr
  Register #(.width(24)) u_R13 (.D(Write_Value), .en(R13_Enab), .Q(r13), .clk(Clock));  // open: clr
  Register #(.width(24)) u_R02 (.D(Write_Value), .en(R02_Enab), .Q(r02), .clk(Clock));  // open: clr
  Register #(.width(24)) u_R06 (.D(Write_Value), .en(R06_Enab), .Q(r06), .clk(Clock));  // open: clr
  Register #(.width(24)) u_R10 (.D(Write_Value), .en(R10_Enab), .Q(r10), .clk(Clock));  // open: clr
  Register #(.width(24)) u_R14 (.D(Write_Value), .en(R14_Enab), .Q(r14), .clk(Clock));  // open: clr
  readRegister readregister_3 (
    .r15(r15), .r14(r14), .r13(r13), .r12(r12), .r11(r11), .r10(r10), .r09(r09), .r08(r08), .r07(r07),
    .r06(r06), .r05(r05), .r04(r04), .r03(r03), .r02(r02), .r01(r01), .r00(r00), .ReadReg(Write_Reg),
    .Output(Reg_3_Value));
  and and_1 (and_1_out, 1'b1, Reg_Write);
  Demultiplexer #(.select(4)) demultiplexer_1 (
    .out1(R01_Enab), .out2(R02_Enab), .out3(R03_Enab), .out4(R04_Enab), .out5(R05_Enab), .out6(R06_Enab),
    .out7(R07_Enab), .out8(R08_Enab), .out9(R09_Enab), .out10(R10_Enab), .out11(R11_Enab), .out12(R12_Enab),
    .out13(R13_Enab), .out14(R14_Enab), .out15(R15_Enab), .in(and_1_out), .sel(Write_Reg));  // open: out0, en
  Register #(.width(24)) u_R03 (.D(Write_Value), .en(R03_Enab), .Q(r03), .clk(Clock));  // open: clr
  Register #(.width(24)) u_R07 (.D(Write_Value), .en(R07_Enab), .Q(r07), .clk(Clock));  // open: clr
  Register #(.width(24)) u_R11 (.D(Write_Value), .en(R11_Enab), .Q(r11), .clk(Clock));  // open: clr
  Register #(.width(24)) u_R15 (.D(Write_Value), .en(R15_Enab), .Q(r15), .clk(Clock));  // open: clr

  // Other names for the same wires on the sheet: clk = Clock; reg1Read[3:0] = Read_Reg_1; reg1Val[23:0] = Reg_1_Value;
  //   reg2Read[3:0] = Read_Reg_2; reg2Val[23:0] = Reg_2_Value; reg3Val[23:0] = Reg_3_Value;
  //   reg3Write[3:0] = Write_Reg; write = Reg_Write; writeVal[23:0] = Write_Value

  // Notes on the sheet:
  //   INPUT PINS
  //   INPUT PROBES
  //   OUTPUT PROBES
  //   OUTPUT PINS
endmodule

module readRegister (
  input  [23:0] r15,
  input  [23:0] r14,
  input  [23:0] r13,
  input  [23:0] r12,
  input  [23:0] r11,
  input  [23:0] r10,
  input  [23:0] r09,
  input  [23:0] r08,
  input  [23:0] r07,
  input  [23:0] r06,
  input  [23:0] r05,
  input  [23:0] r04,
  input  [23:0] r03,
  input  [23:0] r02,
  input  [23:0] r01,
  input  [23:0] r00,
  input  [3:0] ReadReg,
  output [23:0] Output
);

  Multiplexer #(.select(4), .width(24)) multiplexer_1 (
    .in0(r00), .in1(r01), .in2(r02), .in3(r03), .in4(r04), .in5(r05), .in6(r06), .in7(r07), .in8(r08),
    .in9(r09), .in10(r10), .in11(r11), .in12(r12), .in13(r13), .in14(r14), .in15(r15), .out(Output),
    .sel(ReadReg));  // open: en
endmodule
