// Logisim project lab12ALU.circ as structural Verilog: 1 circuit, main circuit ALU
// LAB12-ALU
module ALU (
  input  [31:0] ALU_Source_1,
  input  [31:0] ALU_Source_2,
  input  [2:0] ALU_Control,
  output [31:0] ALU_Result
);

  wire [4:0] Source2_5bit;
  wire [31:0] _000, _001, _010, _011, _100, _101, _110, _111;

  // Probe on ALU_Source_1
  // Probe on ALU_Source_2
  Bit_Extender #(.in_width(32), .out_width(5)) bit_extender_1 (.in(ALU_Source_2), .out(Source2_5bit));
  Shifter #(.width(32)) shifter_1 (.in(ALU_Source_1), .\dist (Source2_5bit), .out(_000));
  Shifter #(.width(32), .shift("lr")) shifter_2 (.in(ALU_Source_1), .\dist (Source2_5bit), .out(_001));
  Shifter #(.width(32), .shift("ar")) shifter_3 (.in(ALU_Source_1), .\dist (Source2_5bit), .out(_010));
  assign _101 = ALU_Source_1 & ALU_Source_2;  // AND_Gate and_1, 32 bits wide
  assign _110 = ALU_Source_1 | ALU_Source_2;  // OR_Gate or_1, 32 bits wide
  assign _111 = ALU_Source_1 ^ ALU_Source_2;  // XOR_Gate xor_1, 32 bits wide
  Shifter #(.width(32), .shift("rl")) shifter_4 (.in(ALU_Source_1), .\dist (Source2_5bit), .out(_011));
  Shifter #(.width(32), .shift("rr")) shifter_5 (.in(ALU_Source_1), .\dist (Source2_5bit), .out(_100));
  // Probe on ALU_Result
  Multiplexer #(.select(3), .width(32), .enable("false")) multiplexer_1 (
    .in0(_000), .in1(_001), .in2(_010), .in3(_011), .in4(_100), .in5(_101), .in6(_110), .in7(_111),
    .out(ALU_Result), .sel(ALU_Control));

  // Other names for the same wires on the sheet: control[2:0] = ALU_Control; result[31:0] = ALU_Result;
  //   source1[31:0] = ALU_Source_1; source2[31:0] = ALU_Source_2

  // Notes on the sheet:
  //   DO NOT CROSS WIRES
  //   OVER THIS BOX
  //   DO NOT CROSS WIRES
  //   OVER THIS BOX
  //   COMPUTE ALL POSSIBLE OPERATIONS
  //   DO NOT CROSS WIRES
  //   OVER THIS BOX
  //   DO NOT CROSS WIRES
  //   OVER THIS BOX
  //   SELECT THE REQUESTED RESULT
  //   DO NOT CROSS WIRES
  //   OVER THIS BOX
endmodule
